# Fritzing sketch ExplorerElectronics (saved by Fritzing 0.9.2b)

parts:
  U1 = Explorer HAT Pro [part_number="Explorer HAT Pro" package=THT]
  LED1 = RGB LED (com. cathode, rgb) [package="5 mm [THT]"]  # not connected
  R1 = Resistor [tolerance=±5% resistance=220 package=THT]  # not connected
  R2 = Resistor [tolerance=±5% resistance=220 package=THT]  # not connected
  R3 = Resistor [tolerance=±5% resistance=220 package=THT]  # not connected
  S1 = Pushbutton [package="[THT]"]
  U2 = Explorer HAT Pro [part_number="Explorer HAT Pro" package=THT]
  POT1 = Breadboard Trimpot  # not connected
  R4 = Photocell (LDR) [package=THT]  # not connected
  LED2 = LED - 5mm [color="Red (633nm)" package="5 mm [THT]"]  # not connected
  U3 = Explorer HAT Pro [part_number="Explorer HAT Pro" package=THT]
  LED3 = LED - 5mm [color="Red (633nm)" package="5 mm [THT]"]  # not connected
  R5 = Resistor [tolerance=±5% resistance=220 package=THT]  # not connected
  U4 = Explorer HAT Pro [part_number="Explorer HAT Pro" package=THT]
  LED4 = RGB LED (com. cathode, rgb) [package="5 mm [THT]"]  # not connected
  R6 = Resistor [tolerance=±5% resistance=220 package=THT]  # not connected
  R7 = Resistor [tolerance=±5% resistance=220 package=THT]  # not connected
  R8 = Resistor [tolerance=±5% resistance=220 package=THT]  # not connected
  U5 = Explorer HAT Pro [part_number="Explorer HAT Pro" package=THT]
  R9 = Resistor [tolerance=±5% resistance=220 package=THT]  # not connected
  LED5 = LED - 5mm [color="Red (633nm)" package="5 mm [THT]"]  # not connected
  POT2 = Breadboard Trimpot  # not connected

nets:
  N1: U1.5v, U1.F7, U1.I7
  N2: U1.C12, U1.E12
  N3: U1.C13, U1.D13, U1.Ground
  N4: U1.C14, U1.E14
  N5: U1.C15, U1.E15
  N6: U1.F5, U1.I5, U1.Input_1
  N7: U1.G12, U1.J12, U1.Output_1
  N8: U1.G14, U1.J14, U1.Output_2
  N9: U1.G15, U1.J15, U1.Output_3
  N10: S1.Pin_1, S1.Pin_2
  N11: S1.Pin_3, S1.Pin_4
  N12: U2.5v, U2.D2, U2.E2
  N13: U2.D3, U2.E3, U2.Analog_1
  N14: U2.D4, U2.E4, U2.F9, U2.I9, U2.Ground
  N15: U2.F6, U2.I6, U2.Analog_4
  N16: U3.5v, U3.F9, U3.J9
  N17: U3.F10, U3.G10
  N18: U3.G14, U3.I14, U3.Output_1
  N19: U4.A12, U4.D12, U4.E12
  N20: U4.A14, U4.D14, U4.E14
  N21: U4.A15, U4.D15, U4.E15
  N22: U4.D13, U4.E13, U4.Ground
  N23: U4.G12, U4.J12, U4.Output_1
  N24: U4.G14, U4.J14, U4.Output_2
  N25: U4.G15, U4.J15, U4.Output_3
  N26: U5.5v, U5.D4, U5.E4, U5.F9, U5.J9
  N27: U5.D5, U5.E5, U5.Analog_1
  N28: U5.D6, U5.E6, U5.Ground
  N29: U5.F10, U5.G10
  N30: U5.G14, U5.I14, U5.Output_1

custom parts:
  Explorer HAT Pro: Explorer HAT Pro with 4 Output and 4 Input connections, 4 Analog Inputs and 2 bi-directional motor channels, plus power and ground.
