# Fritzing sketch ultrasonic-themomin (saved by Fritzing 0.9.3b)
breadboards: 1

parts:
  hc-sr1 = hc-sr04
  R1 = Resistor [tolerance=±5% resistance=2.2k package=THT]
  R2 = Resistor [tolerance=±5% resistance=1k package=THT]
  R3 = Resistor [tolerance=±5% resistance=2.2k package=THT]
  Raspberry_Pi_1 = Raspberry Pi 3 [part_number=RPI-3-V1.2]

nets:
  VCC: hc-sr1.VCC, Raspberry_Pi_1.5V
  N1: hc-sr1.Trig, R1.Pin_0
  N2: hc-sr1.Echo, R2.Pin_0
  GND: hc-sr1.GND, R3.Pin_1, Raspberry_Pi_1.GND
  N3: R1.Pin_1, R2.Pin_1, R3.Pin_0, Raspberry_Pi_1.GPIO23
